# Fritzing sketch midi_Mouse_circuit (saved by Fritzing 0.9.4)
breadboards: 1

parts:
  Arduino_Micro = Arduino Micro (Rev3)
  DIN_6 = mini DIN 6 Connector [package=mini-din6]
  Part1 = Bicolor 8x8 LED Matrix Backpack [part_number=902]
  Part2 = OLED Monochrome 128x64 0.96 inch [part_number=326]

nets:
  GND: Arduino_Micro.GND, DIN_6.3, Part1.GND, Part2.GND
  N1: Arduino_Micro.D2/SDA, Part1.SDA, Part2.MOSI_SDA
  N2: Arduino_Micro.D3/SCL, Part1.SCL, Part2.SCLK_SCK
  N3: Arduino_Micro.D5_PWM, DIN_6.5
  N4: Arduino_Micro.D6_PWM/A7, DIN_6.1, DIN_6.2
  5V: Arduino_Micro.5V, DIN_6.4, Part1.VDD, Part2.VIN

notes:
  Din 6 :
  Green - Data
  Blue - Clock

custom parts:
  Bicolor 8x8 LED Matrix Backpack: This 1.2" bi-color 8x8 LED matrix includes a driver chip for simple control via an I2C interface. It's called a Bicolor LED, but you can have 3 colors total by turning on the red and green LEDs, which creates yellow. That's 3 colors for the price of 2! The backpacks come with address-selection jumpers so you can connect up to eight bicolor matrices on a single I2C bus.
  OLED Monochrome 128x64 0.96 inch: These displays are small, only about 1" diameter, but very readable due to the high contrast of an OLED display. This display is made of 128x64 individual white OLED pixels, each one is turned on or off by the controller chip. Because the display makes its own light, no backlight is required. This reduces the power required to run the OLED and is why the display has such high contrast; we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
